# Fritzing sketch fritzing.motor2 (saved by Fritzing 0.9.4)
breadboards: 1

parts:
  IC1 = L293D [package=THT]
  VCC1 = Battery block 9V
  M2 = DC Motor
  M2_2 = DC Motor
  Raspberry_Pi_3 = Raspberry Pi 3 [part_number=RPI-3-V1.2]

nets:
  N1: IC1.Enable_1, IC1.Enable_2, IC1.+V, Raspberry_Pi_3.5V
  N2: IC1.In_1, Raspberry_Pi_3.GPIO20
  N3: IC1.Out_1_(_Controlled_by_Enable_1_), M2.pin_1
  N4: IC1.0V, VCC1.-, Raspberry_Pi_3.GND
  N5: IC1.Out_2_(_Controlled_by_Enable_1_), M2.pin_2
  N6: IC1.In_2, Raspberry_Pi_3.GPIO8
  N7: IC1.+Vmotor, VCC1.+
  N8: IC1.In_3, Raspberry_Pi_3.GPIO24
  N9: IC1.Out_3_(_Controlled_by_Enable_2_), M2_2.pin_1
  N10: IC1.Out_4_(_Controlled_by_Enable_2_), M2_2.pin_2
  N11: IC1.In_4, Raspberry_Pi_3.GPIO25
